# Fritzing sketch two-capsense-inputs (saved by Fritzing 0.8.7b)
breadboards: 1

parts:
  Part1 = Arduino Uno (Rev3)
  R1 = Resistor [tolerance=±5% resistance=1M package=THT]
  R2 = Resistor [tolerance=±5% resistance=1M package=THT]

nets:
  N1: Part1.D9_PWM, R2.Pin_1
  N2: Part1.D10_PWM/SS, R1.Pin_1, R2.Pin_0
  N3: Part1.D11_PWM/MOSI, R1.Pin_0

notes:
  Paperclip / Copper Foil
